# Fritzing sketch final (saved by Fritzing 0.9.4)
breadboards: 1

parts:
  Part1 = KY-006 Passive Buzzer Module [package="Breakout board"]
  Part2 = KY-011 Two Color LED Module [package="Breakout board"]
  Part3 = MQ-7 breakout
  Part4 = MQ-7 breakout
  Part5 = MQ-7 breakout
  Mod1 = Lipo Battery Pack
  Part6 = Bluetooth HM-10
  Part8 = Arduino Pro Mini (5V)
  R1 = Resistor [tolerance=±5% resistance=220 package="1206 [SMD]"]
  R2 = Resistor [tolerance=±5% resistance=220 package="1206 [SMD]"]

nets:
  GND: Part1.S, Part2.-, Part3.GND, Part4.GND, Part5.GND, Mod1.GND, Part6.GND, Part8.GND
  N1: Part1.-, Part8.D4
  N2: Part2.S, R1.Pin_0
  N3: Part2.Vin, R2.Pin_0
  VCC: Part3.VCC, Part4.VCC, Part5.VCC, Mod1.+5V, Part6.VCC, Part8.VCC
  N4: Part3.AO, Part8.A2
  N5: Part4.AO, Part8.A1
  N6: Part5.AO, Part8.A3
  N7: Part6.RXD, Part8.RXI
  N8: Part6.TXD, Part8.TXO
  N9: Part8.D3, R2.Pin_1
  N10: Part8.D2, R1.Pin_1

custom parts:
  KY-006 Passive Buzzer Module: Passive Piezoelectric Buzzer Module Keyes KY-006, it can produce a range of sound tones depending on the input frequency.
  KY-011 Two Color LED Module: KEYES KY-011 Two Color LED Module consist of a common cathode 3mm red/green LED.
  MQ-7 breakout: SKU: 101282
  Lipo Battery Pack: Micro USB 5V 16340 18650 lithium Battery Shield V3 Wemos ESP32 ESP8266 Module
